// Logisim project CPU.circ as structural Verilog
module Processor (
  input  in_1,
  input  [4:0] in_2,
  input  [4:0] in_3,
  input  [4:0] in_4,
  input  [31:0] in_5,
  input  in_6,
  output [31:0] out_7,
  output [31:0] out_8
);

  wire clock_1_out;

  Clock clock_1 (.out(clock_1_out));
  Register_File register_file_1 (
    .WRITE(in_5), .RS(in_2), .RT(in_3), .RD(in_4), .Register_Write(in_1), .RESET(in_6), .Clock(clock_1_out),
    .out_8(out_7), .out_9(out_8));
endmodule

module Register_File (
  input  [31:0] WRITE,
  input  [4:0] RS,
  input  [4:0] RT,
  input  [4:0] RD,
  input  Register_Write,
  input  RESET,
  input  Clock,
  output [31:0] out_8,
  output [31:0] out_9
);

  wire and_1_out, and_2_out, and_3_out, and_4_out, decoder_1_out0, decoder_1_out1, decoder_1_out2,
       decoder_1_out3, decoder_1_out4, decoder_1_out5, decoder_1_out6, decoder_1_out7, decoder_1_out8,
       decoder_1_out9, decoder_1_out10, decoder_1_out11, decoder_1_out12, decoder_1_out13, decoder_1_out14,
       decoder_1_out15, decoder_1_out16, decoder_1_out17, decoder_1_out18, decoder_1_out19, decoder_1_out20,
       decoder_1_out21, decoder_1_out22, decoder_1_out23, decoder_1_out24, decoder_1_out25, decoder_1_out26,
       decoder_1_out27, decoder_1_out28, decoder_1_out29, decoder_1_out30, decoder_1_out31;
  wire [31:0] R0, R1, R2, R3, R4, R5, R6, R7, R8, R9, R10, R11, R12, R13, R14, R15, R16, R17, R18, R19, R20,
       R21, R22, R23, R24, R25, R26, R27, R28, R29, R30, R31;

  Decoder #(.select(5), .enable("false")) decoder_1 (
    .out0(decoder_1_out0), .out1(decoder_1_out1), .out2(decoder_1_out2), .out3(decoder_1_out3),
    .out4(decoder_1_out4), .out5(decoder_1_out5), .out6(decoder_1_out6), .out7(decoder_1_out7),
    .out8(decoder_1_out8), .out9(decoder_1_out9), .out10(decoder_1_out10), .out11(decoder_1_out11),
    .out12(decoder_1_out12), .out13(decoder_1_out13), .out14(decoder_1_out14), .out15(decoder_1_out15),
    .out16(decoder_1_out16), .out17(decoder_1_out17), .out18(decoder_1_out18), .out19(decoder_1_out19),
    .out20(decoder_1_out20), .out21(decoder_1_out21), .out22(decoder_1_out22), .out23(decoder_1_out23),
    .out24(decoder_1_out24), .out25(decoder_1_out25), .out26(decoder_1_out26), .out27(decoder_1_out27),
    .out28(decoder_1_out28), .out29(decoder_1_out29), .out30(decoder_1_out30), .out31(decoder_1_out31),
    .sel(RD));
  and and_1 (and_1_out, decoder_1_out0, Register_Write);
  and and_2 (and_2_out, decoder_1_out1, Register_Write);
  and and_3 (and_3_out, decoder_1_out2, Register_Write);
  and and_4 (and_4_out, decoder_1_out3, Register_Write);
  Register #(.width(32), .trigger("falling")) register_1 (.D(WRITE), .en(and_1_out), .Q(R0), .clk(Clock), .clr(RESET));
  Register #(.width(32), .trigger("falling")) register_2 (
    .D(WRITE), .en(decoder_1_out4), .Q(R4), .clk(Clock), .clr(RESET));
  Register #(.width(32), .trigger("falling")) register_3 (
    .D(WRITE), .en(decoder_1_out8), .Q(R8), .clk(Clock), .clr(RESET));
  Register #(.width(32), .trigger("falling")) register_4 (
    .D(WRITE), .en(decoder_1_out12), .Q(R12), .clk(Clock), .clr(RESET));
  Register #(.width(32), .trigger("falling")) register_5 (
    .D(WRITE), .en(decoder_1_out16), .Q(R16), .clk(Clock), .clr(RESET));
  Register #(.width(32), .trigger("falling")) register_6 (
    .D(WRITE), .en(decoder_1_out20), .Q(R20), .clk(Clock), .clr(RESET));
  Register #(.width(32), .trigger("falling")) register_7 (
    .D(WRITE), .en(decoder_1_out24), .Q(R24), .clk(Clock), .clr(RESET));
  Register #(.width(32), .trigger("falling")) register_8 (
    .D(WRITE), .en(decoder_1_out28), .Q(R28), .clk(Clock), .clr(RESET));
  Register #(.width(32), .trigger("falling")) register_9 (.D(WRITE), .en(and_2_out), .Q(R1), .clk(Clock), .clr(RESET));
  Register #(.width(32), .trigger("falling")) register_10 (
    .D(WRITE), .en(decoder_1_out5), .Q(R5), .clk(Clock), .clr(RESET));
  Register #(.width(32), .trigger("falling")) register_11 (
    .D(WRITE), .en(decoder_1_out9), .Q(R9), .clk(Clock), .clr(RESET));
  Register #(.width(32), .trigger("falling")) register_12 (
    .D(WRITE), .en(decoder_1_out13), .Q(R13), .clk(Clock), .clr(RESET));
  Register #(.width(32), .trigger("falling")) register_13 (
    .D(WRITE), .en(decoder_1_out17), .Q(R17), .clk(Clock), .clr(RESET));
  Register #(.width(32), .trigger("falling")) register_14 (
    .D(WRITE), .en(decoder_1_out21), .Q(R21), .clk(Clock), .clr(RESET));
  Register #(.width(32), .trigger("falling")) register_15 (
    .D(WRITE), .en(decoder_1_out25), .Q(R25), .clk(Clock), .clr(RESET));
  Register #(.width(32), .trigger("falling")) register_16 (
    .D(WRITE), .en(decoder_1_out29), .Q(R29), .clk(Clock), .clr(RESET));
  Register #(.width(32), .trigger("falling")) register_17 (.D(WRITE), .en(and_3_out), .Q(R2), .clk(Clock), .clr(RESET));
  Register #(.width(32), .trigger("falling")) register_18 (
    .D(WRITE), .en(decoder_1_out6), .Q(R6), .clk(Clock), .clr(RESET));
  Register #(.width(32), .trigger("falling")) register_19 (
    .D(WRITE), .en(decoder_1_out10), .Q(R10), .clk(Clock), .clr(RESET));
  Register #(.width(32), .trigger("falling")) register_20 (
    .D(WRITE), .en(decoder_1_out14), .Q(R14), .clk(Clock), .clr(RESET));
  Register #(.width(32), .trigger("falling")) register_21 (
    .D(WRITE), .en(decoder_1_out18), .Q(R18), .clk(Clock), .clr(RESET));
  Register #(.width(32), .trigger("falling")) register_22 (
    .D(WRITE), .en(decoder_1_out22), .Q(R22), .clk(Clock), .clr(RESET));
  Register #(.width(32), .trigger("falling")) register_23 (
    .D(WRITE), .en(decoder_1_out26), .Q(R26), .clk(Clock), .clr(RESET));
  Register #(.width(32), .trigger("falling")) register_24 (
    .D(WRITE), .en(decoder_1_out30), .Q(R30), .clk(Clock), .clr(RESET));
  Register #(.width(32), .trigger("falling")) register_25 (.D(WRITE), .en(and_4_out), .Q(R3), .clk(Clock), .clr(RESET));
  Register #(.width(32), .trigger("falling")) register_26 (
    .D(WRITE), .en(decoder_1_out7), .Q(R7), .clk(Clock), .clr(RESET));
  Register #(.width(32), .trigger("falling")) register_27 (
    .D(WRITE), .en(decoder_1_out11), .Q(R11), .clk(Clock), .clr(RESET));
  Register #(.width(32), .trigger("falling")) register_28 (
    .D(WRITE), .en(decoder_1_out15), .Q(R15), .clk(Clock), .clr(RESET));
  Register #(.width(32), .trigger("falling")) register_29 (
    .D(WRITE), .en(decoder_1_out19), .Q(R19), .clk(Clock), .clr(RESET));
  Register #(.width(32), .trigger("falling")) register_30 (
    .D(WRITE), .en(decoder_1_out23), .Q(R23), .clk(Clock), .clr(RESET));
  Register #(.width(32), .trigger("falling")) register_31 (
    .D(WRITE), .en(decoder_1_out27), .Q(R27), .clk(Clock), .clr(RESET));
  Register #(.width(32), .trigger("falling")) register_32 (
    .D(WRITE), .en(decoder_1_out31), .Q(R31), .clk(Clock), .clr(RESET));
  Multiplexer #(.select(5), .width(32), .enable("false")) multiplexer_1 (
    .in0(R0), .in1(R1), .in2(R2), .in3(R3), .in4(R4), .in5(R5), .in6(R6), .in7(R7), .in8(R16), .in9(R17),
    .in10(R18), .in11(R19), .in12(R20), .in13(R21), .in14(R22), .in15(R23), .in16(R8), .in17(R9), .in18(R10),
    .in19(R11), .in20(R12), .in21(R13), .in22(R14), .in23(R15), .in24(R24), .in25(R25), .in26(R26),
    .in27(R27), .in28(R28), .in29(R29), .in30(R30), .in31(R31), .out(out_8), .sel(RS));
  Multiplexer #(.select(5), .width(32), .enable("false")) multiplexer_2 (
    .in0(R0), .in1(R1), .in2(R2), .in3(R3), .in4(R4), .in5(R5), .in6(R6), .in7(R7), .in8(R16), .in9(R17),
    .in10(R18), .in11(R19), .in12(R20), .in13(R21), .in14(R22), .in15(R23), .in16(R8), .in17(R9), .in18(R10),
    .in19(R11), .in20(R12), .in21(R13), .in22(R14), .in23(R15), .in24(R24), .in25(R25), .in26(R26),
    .in27(R27), .in28(R28), .in29(R29), .in30(R30), .in31(R31), .out(out_9), .sel(RT));

  // Other names for the same wires on the sheet: RS_TNL[4:0] = RS; RT_TNL[4:0] = RT
endmodule
