// Logisim project CPU.circ as structural Verilog: 4 circuits, main circuit Processor
module Processor (
  input  RESET,
  input  INSTRUCTION_CLEAR,
  input  [23:0] in_3,
  input  in_4,
  input  in_5,
  output [31:0] out_6,
  output [31:0] out_7,
  output [31:0] out_8
);

  wire alu_1_out_4, and_1_out, CLK, ctrl_1_alu_s, ctrl_1_b, ctrl_1_j, ctrl_1_mem_to_reg, ctrl_1_mem_wrt,
       ctrl_1_reg_dst, ctrl_1_reg_wrt, ctrl_1_sign_ext;
  wire [2:0] ctrl_1_alu_op;
  wire [4:0] ctrl_1_rd, ctrl_1_rs, ctrl_1_rt, multiplexer_1_out;
  wire [15:0] ctrl_1_imm;
  wire [23:0] bit_extender_1_out, bit_extender_5_out;
  wire [25:0] ctrl_1_jump;
  wire [31:0] adder_1_out, adder_2_out, alu_1_out, bit_extender_2_out, bit_extender_3_out,
       bit_extender_4_out, multiplexer_2_out, multiplexer_3_out, multiplexer_4_out, multiplexer_5_out,
       multiplexer_6_out, PC_q, ram_1_data, ram_2_data;

  Clock CLOCK (.out(CLK));
  Register #(.width(32), .trigger("falling")) PC (.D(multiplexer_5_out), .Q(PC_q), .clk(CLK), .clr(RESET));  // open: en
  Bit_Extender #(.in_width(32), .out_width(24)) bit_extender_1 (.in(PC_q), .out(bit_extender_1_out));
  CTRL ctrl_1 (
    .in_1(ram_1_data), .ALU_OP(ctrl_1_alu_op), .Reg_Dst(ctrl_1_reg_dst), .ALU_S(ctrl_1_alu_s), .B(ctrl_1_b),
    .J(ctrl_1_j), .Mem_Wrt(ctrl_1_mem_wrt), .Mem_To_Reg(ctrl_1_mem_to_reg), .Reg_Wrt(ctrl_1_reg_wrt),
    .Sign_Ext(ctrl_1_sign_ext), .IMM(ctrl_1_imm), .RD(ctrl_1_rd), .RT(ctrl_1_rt), .RS(ctrl_1_rs),
    .JUMP(ctrl_1_jump));  // open: SHAMT
  RAM #(.addrWidth(24), .dataWidth(32)) ram_1 (
    .addr(bit_extender_1_out), .data(ram_1_data), .clk(CLK), .clr(INSTRUCTION_CLEAR));  // open: sel, ld
  Multiplexer #(.width(5), .enable("false")) multiplexer_1 (
    .in0(ctrl_1_rt), .in1(ctrl_1_rd), .out(multiplexer_1_out), .sel(ctrl_1_reg_dst));
  Adder #(.width(32)) adder_1 (.a(PC_q), .b(32'h1), .out(adder_1_out));  // open: cin, cout
  assign bit_extender_2_out = {{6{1'b0}}, ctrl_1_jump};  // Bit_Extender bit_extender_2
  Register_File register_file_1 (
    .DATA(multiplexer_6_out), .RS(ctrl_1_rs), .RT(ctrl_1_rt), .RD(multiplexer_1_out),
    .Register_Write(ctrl_1_reg_wrt), .Clock(CLK), .out_8(out_6), .RESET(RESET), .out_9(out_7));
  RAM #(.addrWidth(24), .dataWidth(32)) ram_2 (
    .addr(in_3), .data(ram_2_data), .clk(in_4), .ld(in_5));  // open: sel, clr
  assign bit_extender_3_out = {{16{1'b0}}, ctrl_1_imm};  // Bit_Extender bit_extender_3
  assign bit_extender_4_out = {{16{ctrl_1_imm[15]}}, ctrl_1_imm};  // Bit_Extender bit_extender_4
  Multiplexer #(.width(32), .enable("false")) multiplexer_2 (
    .in0(bit_extender_3_out), .in1(bit_extender_4_out), .out(multiplexer_2_out), .sel(ctrl_1_sign_ext));
  Adder #(.width(32)) adder_2 (.a(adder_1_out), .b(multiplexer_2_out), .out(adder_2_out));  // open: cin, cout
  ALU alu_1 (.A(out_6), .B(multiplexer_3_out), .OUT(alu_1_out), .in_3(ctrl_1_alu_op), .out_4(alu_1_out_4));
  Multiplexer #(.width(32), .enable("false")) multiplexer_3 (
    .in0(out_7), .in1(multiplexer_2_out), .out(multiplexer_3_out), .sel(ctrl_1_alu_s));
  Multiplexer #(.width(32), .enable("false")) multiplexer_4 (
    .in0(adder_1_out), .in1(adder_2_out), .out(multiplexer_4_out), .sel(and_1_out));
  and and_1 (and_1_out, ctrl_1_b, alu_1_out_4);
  Bit_Extender #(.in_width(32), .out_width(24)) bit_extender_5 (.in(alu_1_out), .out(bit_extender_5_out));
  Multiplexer #(.width(32), .enable("false")) multiplexer_5 (
    .in0(multiplexer_4_out), .in1(bit_extender_2_out), .out(multiplexer_5_out), .sel(ctrl_1_j));
  RAM #(.addrWidth(24), .dataWidth(32), .bus("separate")) ram_3 (
    .addr(bit_extender_5_out), .din(out_7), .data(out_8), .str(ctrl_1_mem_wrt), .clk(CLK), .ld(1'b1),
    .clr(RESET));  // open: sel
  Multiplexer #(.width(32), .enable("false")) multiplexer_6 (
    .in0(alu_1_out), .in1(out_8), .out(multiplexer_6_out), .sel(ctrl_1_mem_to_reg));

  // Notes on the sheet:
  //   INST. MEM.
  //   RegDst
  //   Reg Write
  //   ALU S
  //   Branch
  //   Zero
  //   Jump
  //   Mem Write
  //   Mem to Reg
  //   BORDER
endmodule

module ALU (
  input  [31:0] A,
  input  [31:0] B,
  input  [2:0] in_3,
  output out_4,
  output [31:0] OUT
);

  wire [31:0] adder_1_out, and_1_out, or_1_out, subtractor_1_out;

  Adder #(.width(32)) adder_1 (.a(A), .b(B), .out(adder_1_out));  // open: cin, cout
  Subtractor #(.width(32)) subtractor_1 (.a(A), .b(B), .out(subtractor_1_out));  // open: bin, bout
  assign or_1_out = A | B;  // OR_Gate or_1, 32 bits wide
  assign and_1_out = A & B;  // AND_Gate and_1, 32 bits wide
  Multiplexer #(.select(3), .width(32), .enable("false")) multiplexer_1 (
    .in0(adder_1_out), .in1(subtractor_1_out), .in2(or_1_out), .in4(and_1_out), .out(OUT), .sel(in_3));  // open: in3, in5, in6, in7
  nor nor_1 (out_4, subtractor_1_out[0], subtractor_1_out[1], subtractor_1_out[2], subtractor_1_out[3], subtractor_1_out[4], subtractor_1_out[5], subtractor_1_out[6], subtractor_1_out[7], subtractor_1_out[8], subtractor_1_out[9], subtractor_1_out[10], subtractor_1_out[11], subtractor_1_out[12], subtractor_1_out[13], subtractor_1_out[14], subtractor_1_out[15], subtractor_1_out[16], subtractor_1_out[17], subtractor_1_out[18], subtractor_1_out[19], subtractor_1_out[20], subtractor_1_out[21], subtractor_1_out[22], subtractor_1_out[23], subtractor_1_out[24], subtractor_1_out[25], subtractor_1_out[26], subtractor_1_out[27], subtractor_1_out[28], subtractor_1_out[29], subtractor_1_out[30], subtractor_1_out[31]);
endmodule

module CTRL (
  input  [31:0] in_1,
  output [2:0] ALU_OP,
  output Reg_Dst,
  output ALU_S,
  output B,
  output Sign_Ext,
  output J,
  output Mem_Wrt,
  output [4:0] SHAMT,
  output [15:0] IMM,
  output [4:0] RD,
  output Mem_To_Reg,
  output [4:0] RT,
  output [25:0] JUMP,
  output Reg_Wrt,
  output [4:0] RS
);

  wire or_2_out, or_3_out;
  wire [1:0] or_1_out;
  wire [2:0] bit_extender_1_out, bit_extender_2_out, multiplexer_2_out;

  Multiplexer #(.select(2), .enable("false")) multiplexer_1 (
    .in0(1'b0), .in1(1'b1), .in2(1'b1), .in3(1'b0), .out(Sign_Ext), .sel({in_1[31], in_1[26]}));
  Bit_Extender #(.in_width(6), .out_width(3)) bit_extender_1 (.in(in_1[31:26]), .out(bit_extender_1_out));
  or or_1 (or_1_out[0], or_2_out, in_1[26]);
  or or_2 (or_2_out, in_1[27], in_1[28], in_1[29], in_1[30]);
  or or_3 (or_3_out, in_1[27], in_1[28], in_1[29], in_1[30]);
  or or_4 (or_1_out[1], in_1[31], or_3_out);
  Multiplexer #(.select(2), .width(3), .enable("false")) multiplexer_2 (
    .in1(3'b000), .in2(3'b100), .in3(bit_extender_1_out), .out(multiplexer_2_out), .sel(or_1_out));  // open: in0
  Bit_Extender #(.in_width(6), .out_width(3)) bit_extender_2 (.in(in_1[5:0]), .out(bit_extender_2_out));
  nor nor_1 (Reg_Dst, in_1[26], in_1[27], in_1[28], in_1[29], in_1[30], in_1[31]);
  or or_5 (ALU_S, in_1[26], in_1[27], in_1[28], in_1[29], in_1[30], in_1[31]);
  and and_1 (B, ~in_1[26], ~in_1[27], ~in_1[28], ~in_1[29], ~in_1[30], in_1[31]);  // AND_Gate
  and and_2 (J, in_1[26], in_1[27], in_1[28], in_1[29], in_1[30], in_1[31]);
  and and_3 (Mem_Wrt, ~in_1[26], ~in_1[27], ~in_1[28], ~in_1[29], in_1[30], ~in_1[31]);  // AND_Gate
  and and_4 (Mem_To_Reg, ~in_1[26], ~in_1[27], ~in_1[28], in_1[29], ~in_1[30], ~in_1[31]);  // AND_Gate
  nor nor_2 (Reg_Wrt, in_1[30], in_1[31]);
  Multiplexer #(.width(3), .enable("false")) multiplexer_3 (
    .in0(multiplexer_2_out), .in1(bit_extender_2_out), .out(ALU_OP), .sel(Reg_Dst));

  assign IMM = in_1[15:0];
  assign JUMP = in_1[25:0];
  assign RD = in_1[15:11];
  assign RS = in_1[25:21];
  assign RT = in_1[20:16];
  assign SHAMT = in_1[10:6];

  // Other names for the same wires on the sheet: OP[5:0] = in_1[31:26]; FUNC[5:0] = in_1[5:0]
endmodule

module Register_File (
  input  [31:0] DATA,
  input  [4:0] RS,
  input  [4:0] RT,
  input  [4:0] RD,
  input  Register_Write,
  input  RESET,
  input  Clock,
  output [31:0] out_8,
  output [31:0] out_9
);

  wire and_1_out, and_2_out, and_3_out, and_4_out, and_5_out, and_6_out, and_7_out, and_8_out, and_9_out,
       and_10_out, and_11_out, and_12_out, and_13_out, and_14_out, and_15_out, and_16_out, and_17_out,
       and_18_out, and_19_out, and_20_out, and_21_out, and_22_out, and_23_out, and_24_out, and_25_out,
       and_26_out, and_27_out, and_28_out, and_29_out, and_30_out, and_31_out, and_32_out, decoder_1_out0,
       decoder_1_out1, decoder_1_out2, decoder_1_out3, decoder_1_out4, decoder_1_out5, decoder_1_out6,
       decoder_1_out7, decoder_1_out8, decoder_1_out9, decoder_1_out10, decoder_1_out11, decoder_1_out12,
       decoder_1_out13, decoder_1_out14, decoder_1_out15, decoder_1_out16, decoder_1_out17, decoder_1_out18,
       decoder_1_out19, decoder_1_out20, decoder_1_out21, decoder_1_out22, decoder_1_out23, decoder_1_out24,
       decoder_1_out25, decoder_1_out26, decoder_1_out27, decoder_1_out28, decoder_1_out29, decoder_1_out30,
       decoder_1_out31;
  wire [31:0] R0, R1, R2, R3, R4, R5, R6, R7, R8, R9, R10, R11, R12, R13, R14, R15, R16, R17, R18, R19, R20,
       R21, R22, R23, R24, R25, R26, R27, R28, R29, R30, R31;

  Decoder #(.select(5), .enable("false")) decoder_1 (
    .out0(decoder_1_out0), .out1(decoder_1_out1), .out2(decoder_1_out2), .out3(decoder_1_out3),
    .out4(decoder_1_out4), .out5(decoder_1_out5), .out6(decoder_1_out6), .out7(decoder_1_out7),
    .out8(decoder_1_out8), .out9(decoder_1_out9), .out10(decoder_1_out10), .out11(decoder_1_out11),
    .out12(decoder_1_out12), .out13(decoder_1_out13), .out14(decoder_1_out14), .out15(decoder_1_out15),
    .out16(decoder_1_out16), .out17(decoder_1_out17), .out18(decoder_1_out18), .out19(decoder_1_out19),
    .out20(decoder_1_out20), .out21(decoder_1_out21), .out22(decoder_1_out22), .out23(decoder_1_out23),
    .out24(decoder_1_out24), .out25(decoder_1_out25), .out26(decoder_1_out26), .out27(decoder_1_out27),
    .out28(decoder_1_out28), .out29(decoder_1_out29), .out30(decoder_1_out30), .out31(decoder_1_out31),
    .sel(RD));
  and and_1 (and_1_out, Register_Write, decoder_1_out0);
  and and_2 (and_2_out, Register_Write, decoder_1_out1);
  and and_3 (and_3_out, Register_Write, decoder_1_out2);
  and and_4 (and_4_out, Register_Write, decoder_1_out3);
  and and_5 (and_5_out, Register_Write, decoder_1_out4);
  and and_6 (and_6_out, Register_Write, decoder_1_out5);
  and and_7 (and_7_out, Register_Write, decoder_1_out6);
  and and_8 (and_8_out, Register_Write, decoder_1_out7);
  and and_9 (and_9_out, Register_Write, decoder_1_out8);
  and and_10 (and_10_out, Register_Write, decoder_1_out9);
  and and_11 (and_11_out, Register_Write, decoder_1_out10);
  and and_12 (and_12_out, Register_Write, decoder_1_out11);
  and and_13 (and_13_out, Register_Write, decoder_1_out12);
  and and_14 (and_14_out, Register_Write, decoder_1_out13);
  and and_15 (and_15_out, Register_Write, decoder_1_out14);
  and and_16 (and_16_out, Register_Write, decoder_1_out15);
  and and_17 (and_17_out, decoder_1_out16, Register_Write);
  and and_18 (and_18_out, decoder_1_out17, Register_Write);
  and and_19 (and_19_out, decoder_1_out18, Register_Write);
  and and_20 (and_20_out, decoder_1_out19, Register_Write);
  and and_21 (and_21_out, decoder_1_out20, Register_Write);
  and and_22 (and_22_out, decoder_1_out21, Register_Write);
  and and_23 (and_23_out, decoder_1_out22, Register_Write);
  and and_24 (and_24_out, decoder_1_out23, Register_Write);
  and and_25 (and_25_out, decoder_1_out24, Register_Write);
  and and_26 (and_26_out, decoder_1_out25, Register_Write);
  and and_27 (and_27_out, decoder_1_out26, Register_Write);
  and and_28 (and_28_out, decoder_1_out27, Register_Write);
  and and_29 (and_29_out, decoder_1_out28, Register_Write);
  and and_30 (and_30_out, decoder_1_out29, Register_Write);
  and and_31 (and_31_out, decoder_1_out30, Register_Write);
  and and_32 (and_32_out, decoder_1_out31, Register_Write);
  Register #(.width(32), .trigger("falling")) register_1 (.D(DATA), .en(and_1_out), .Q(R0), .clk(Clock), .clr(RESET));
  Register #(.width(32), .trigger("falling")) register_2 (.D(DATA), .en(and_5_out), .Q(R4), .clk(Clock), .clr(RESET));
  Register #(.width(32), .trigger("falling")) register_3 (.D(DATA), .en(and_9_out), .Q(R8), .clk(Clock), .clr(RESET));
  Register #(.width(32), .trigger("falling")) register_4 (.D(DATA), .en(and_13_out), .Q(R12), .clk(Clock), .clr(RESET));
  Register #(.width(32), .trigger("falling")) register_5 (.D(DATA), .en(and_17_out), .Q(R16), .clk(Clock), .clr(RESET));
  Register #(.width(32), .trigger("falling")) register_6 (.D(DATA), .en(and_21_out), .Q(R20), .clk(Clock), .clr(RESET));
  Register #(.width(32), .trigger("falling")) register_7 (.D(DATA), .en(and_25_out), .Q(R24), .clk(Clock), .clr(RESET));
  Register #(.width(32), .trigger("falling")) register_8 (.D(DATA), .en(and_29_out), .Q(R28), .clk(Clock), .clr(RESET));
  Register #(.width(32), .trigger("falling")) register_9 (.D(DATA), .en(and_2_out), .Q(R1), .clk(Clock), .clr(RESET));
  Register #(.width(32), .trigger("falling")) register_10 (.D(DATA), .en(and_6_out), .Q(R5), .clk(Clock), .clr(RESET));
  Register #(.width(32), .trigger("falling")) register_11 (.D(DATA), .en(and_10_out), .Q(R9), .clk(Clock), .clr(RESET));
  Register #(.width(32), .trigger("falling")) register_12 (
    .D(DATA), .en(and_14_out), .Q(R13), .clk(Clock), .clr(RESET));
  Register #(.width(32), .trigger("falling")) register_13 (
    .D(DATA), .en(and_18_out), .Q(R17), .clk(Clock), .clr(RESET));
  Register #(.width(32), .trigger("falling")) register_14 (
    .D(DATA), .en(and_22_out), .Q(R21), .clk(Clock), .clr(RESET));
  Register #(.width(32), .trigger("falling")) register_15 (
    .D(DATA), .en(and_26_out), .Q(R25), .clk(Clock), .clr(RESET));
  Register #(.width(32), .trigger("falling")) register_16 (
    .D(DATA), .en(and_30_out), .Q(R29), .clk(Clock), .clr(RESET));
  Register #(.width(32), .trigger("falling")) register_17 (.D(DATA), .en(and_3_out), .Q(R2), .clk(Clock), .clr(RESET));
  Register #(.width(32), .trigger("falling")) register_18 (.D(DATA), .en(and_7_out), .Q(R6), .clk(Clock), .clr(RESET));
  Register #(.width(32), .trigger("falling")) register_19 (
    .D(DATA), .en(and_11_out), .Q(R10), .clk(Clock), .clr(RESET));
  Register #(.width(32), .trigger("falling")) register_20 (
    .D(DATA), .en(and_15_out), .Q(R14), .clk(Clock), .clr(RESET));
  Register #(.width(32), .trigger("falling")) register_21 (
    .D(DATA), .en(and_19_out), .Q(R18), .clk(Clock), .clr(RESET));
  Register #(.width(32), .trigger("falling")) register_22 (
    .D(DATA), .en(and_23_out), .Q(R22), .clk(Clock), .clr(RESET));
  Register #(.width(32), .trigger("falling")) register_23 (
    .D(DATA), .en(and_27_out), .Q(R26), .clk(Clock), .clr(RESET));
  Register #(.width(32), .trigger("falling")) register_24 (
    .D(DATA), .en(and_31_out), .Q(R30), .clk(Clock), .clr(RESET));
  Register #(.width(32), .trigger("falling")) register_25 (.D(DATA), .en(and_4_out), .Q(R3), .clk(Clock), .clr(RESET));
  Register #(.width(32), .trigger("falling")) register_26 (.D(DATA), .en(and_8_out), .Q(R7), .clk(Clock), .clr(RESET));
  Register #(.width(32), .trigger("falling")) register_27 (
    .D(DATA), .en(and_12_out), .Q(R11), .clk(Clock), .clr(RESET));
  Register #(.width(32), .trigger("falling")) register_28 (
    .D(DATA), .en(and_16_out), .Q(R15), .clk(Clock), .clr(RESET));
  Register #(.width(32), .trigger("falling")) register_29 (
    .D(DATA), .en(and_20_out), .Q(R19), .clk(Clock), .clr(RESET));
  Register #(.width(32), .trigger("falling")) register_30 (
    .D(DATA), .en(and_24_out), .Q(R23), .clk(Clock), .clr(RESET));
  Register #(.width(32), .trigger("falling")) register_31 (
    .D(DATA), .en(and_28_out), .Q(R27), .clk(Clock), .clr(RESET));
  Register #(.width(32), .trigger("falling")) register_32 (
    .D(DATA), .en(and_32_out), .Q(R31), .clk(Clock), .clr(RESET));
  Multiplexer #(.select(5), .width(32), .enable("false")) multiplexer_1 (
    .in0(R0), .in1(R1), .in2(R2), .in3(R3), .in4(R4), .in5(R5), .in6(R6), .in7(R7), .in8(R8), .in9(R9),
    .in10(R10), .in11(R11), .in12(R12), .in13(R13), .in14(R14), .in15(R15), .in16(R16), .in17(R17),
    .in18(R18), .in19(R19), .in20(R20), .in21(R21), .in22(R22), .in23(R23), .in24(R24), .in25(R25),
    .in26(R26), .in27(R27), .in28(R28), .in29(R29), .in30(R30), .in31(R31), .out(out_8), .sel(RS));
  Multiplexer #(.select(5), .width(32), .enable("false")) multiplexer_2 (
    .in0(R0), .in1(R1), .in2(R2), .in3(R3), .in4(R4), .in5(R5), .in6(R6), .in7(R7), .in8(R8), .in9(R9),
    .in10(R10), .in11(R11), .in12(R12), .in13(R13), .in14(R14), .in15(R15), .in16(R16), .in17(R17),
    .in18(R18), .in19(R19), .in20(R20), .in21(R21), .in22(R22), .in23(R23), .in24(R24), .in25(R25),
    .in26(R26), .in27(R27), .in28(R28), .in29(R29), .in30(R30), .in31(R31), .out(out_9), .sel(RT));

  // Other names for the same wires on the sheet: RS_TNL[4:0] = RS; RT_TNL[4:0] = RT
endmodule
